# Fritzing sketch verkabelung (saved by Fritzing 0.9.3b)

parts:
  Bauteil1 = Arduino Mega 2560 (Rev3)
  S1 = H-Bridge with L298N
  M1 = DC Motor
  M2 = DC Motor
  M3 = DC Motor
  M4 = DC Motor
  U1 = LIPO-2000mAh [package=lipo-2000]
  U2 = LIPO-1000mAh [package=lipo-1000]
  J1 = Basic Servo

nets:
  5V: Bauteil1.5V, S1.5V, J1.vcc
  GND: Bauteil1.GND, S1.GND, U1.+, U2.+, J1.gnd
  N1: Bauteil1.VIN, U2.-
  N2: Bauteil1.D5_PWM, J1.pulse
  N3: S1.12V, U1.-
  N4: S1.M1-01, M1.pin_2, M2.pin_2
  N5: S1.M1-02, M1.pin_1, M2.pin_1
  N6: S1.M2-01, M3.pin_2, M4.pin_2
  N7: S1.M2-02, M3.pin_1, M4.pin_1

custom parts:
  H-Bridge with L298N: h-bridge
